// Logisim project amulet.circ as structural Verilog: 1 circuit, main circuit alu
module alu (
  input  [7:0] a,
  input  [7:0] b,
  output [7:0] y
);


  // Notes on the sheet:
  //   add
  //   negate
  //   inc
  //   XOR
  //   dec
  //   AND
  //   OR
endmodule
