// Logisim project chapter1.circ as structural Verilog: 12 circuits, main circuit NAND
module NAND (
  input  a,
  input  b,
  output out
);

  nand nand_1 (out, a, b);
endmodule

module NOT (
  input  in,
  output out
);

  nand nand_1 (out, in, in);
endmodule

module AND (
  input  a,
  input  b,
  output out
);

  wire nand_1_out;

  nand nand_1 (nand_1_out, a, b);
  nand nand_2 (out, nand_1_out, nand_1_out);
endmodule

module OR (
  input  a,
  input  b,
  output out
);

  wire nand_1_out, nand_2_out;

  nand nand_1 (nand_1_out, a, a);
  nand nand_2 (nand_2_out, b, b);
  nand nand_3 (out, nand_1_out, nand_2_out);
endmodule

module XOR (
  input  a,
  input  b,
  output out
);

  wire nand_1_out, nand_2_out, nand_3_out, nand_4_out, nand_5_out;

  nand nand_1 (nand_1_out, a, b);
  nand nand_2 (nand_2_out, a, a);
  nand nand_3 (nand_3_out, b, b);
  nand nand_4 (nand_4_out, nand_2_out, nand_3_out);
  nand nand_5 (nand_5_out, nand_1_out, nand_4_out);
  nand nand_6 (out, nand_5_out, nand_5_out);

  // Notes on the sheet:
  //   NAND
  //   OR
  //   AND
endmodule

module MUX (
  input  a,
  input  sel,
  input  b,
  output out
);

  wire nand_1_out, nand_2_out, nand_3_out, nand_4_out, nand_5_out, nand_6_out, nand_7_out;

  nand nand_1 (nand_1_out, sel, sel);
  nand nand_2 (nand_2_out, a, nand_1_out);
  nand nand_3 (nand_3_out, sel, b);
  nand nand_4 (nand_4_out, nand_2_out, nand_2_out);
  nand nand_5 (nand_5_out, nand_3_out, nand_3_out);
  nand nand_6 (nand_6_out, nand_4_out, nand_4_out);
  nand nand_7 (nand_7_out, nand_5_out, nand_5_out);
  nand nand_8 (out, nand_6_out, nand_7_out);

  // Notes on the sheet:
  //   NOT
  //   AND
  //   AND
  //   OR
endmodule

module DMUX (
  input  sel,
  input  in,
  output a,
  output b
);

  wire nand_1_out, nand_2_out, nand_3_out;

  nand nand_1 (nand_1_out, sel, sel);
  nand nand_2 (nand_2_out, nand_1_out, in);
  nand nand_3 (nand_3_out, sel, in);
  nand nand_4 (a, nand_2_out, nand_2_out);
  nand nand_5 (b, nand_3_out, nand_3_out);

  // Notes on the sheet:
  //   NOT
  //   AND
  //   AND
endmodule

module _8_WAY_OR (
  input  in_0,
  input  in_1,
  input  in_2,
  input  in_3,
  input  in_4,
  input  in_5,
  input  in_6,
  input  in_7,
  output out
);

  wire nand_1_out, nand_2_out, nand_3_out, nand_4_out, nand_5_out, nand_6_out, nand_7_out, nand_8_out,
       nand_9_out, nand_10_out, nand_11_out, nand_12_out, nand_13_out, nand_14_out, nand_15_out, nand_16_out,
       nand_17_out, nand_18_out, nand_19_out, nand_20_out;

  nand nand_1 (nand_1_out, in_0, in_0);
  nand nand_2 (nand_2_out, in_1, in_1);
  nand nand_3 (nand_3_out, in_2, in_2);
  nand nand_4 (nand_4_out, in_3, in_3);
  nand nand_5 (nand_5_out, in_4, in_4);
  nand nand_6 (nand_6_out, in_5, in_5);
  nand nand_7 (nand_7_out, in_6, in_6);
  nand nand_8 (nand_8_out, in_7, in_7);
  nand nand_9 (nand_9_out, nand_1_out, nand_2_out);
  nand nand_10 (nand_10_out, nand_3_out, nand_4_out);
  nand nand_11 (nand_11_out, nand_5_out, nand_6_out);
  nand nand_12 (nand_12_out, nand_7_out, nand_8_out);
  nand nand_13 (nand_13_out, nand_9_out, nand_9_out);
  nand nand_14 (nand_14_out, nand_10_out, nand_10_out);
  nand nand_15 (nand_15_out, nand_11_out, nand_11_out);
  nand nand_16 (nand_16_out, nand_12_out, nand_12_out);
  nand nand_17 (nand_17_out, nand_13_out, nand_14_out);
  nand nand_18 (nand_18_out, nand_15_out, nand_16_out);
  nand nand_19 (nand_19_out, nand_17_out, nand_17_out);
  nand nand_20 (nand_20_out, nand_18_out, nand_18_out);
  nand nand_21 (out, nand_19_out, nand_20_out);
endmodule

module _4_WAY_MUX_16 (
  input  [15:0] a,
  input  [15:0] b,
  input  [15:0] c,
  input  [15:0] d,
  input  sel_0,
  input  sel_1,
  output [15:0] out
);

  wire not_1_out, not_2_out;
  wire [15:0] a0_out, and_1_out, and_2_out, and_3_out, and_4_out, and_5_out, bit_extender_1_out,
       bit_extender_2_out, bit_extender_3_out, bit_extender_4_out, or_1_out, or_2_out;

  not not_1 (not_1_out, sel_0);
  not not_2 (not_2_out, sel_1);
  assign bit_extender_1_out = {{15{not_1_out}}, not_1_out};  // Bit_Extender bit_extender_1
  assign bit_extender_2_out = {{15{sel_0}}, sel_0};  // Bit_Extender bit_extender_2
  assign bit_extender_3_out = {{15{not_2_out}}, not_2_out};  // Bit_Extender bit_extender_3
  assign bit_extender_4_out = {{15{sel_1}}, sel_1};  // Bit_Extender bit_extender_4
  and a0 (a0_out[0], a[0], not_1_out);
  and a1 (a0_out[1], a[1], not_1_out);
  and a2 (a0_out[2], a[2], not_1_out);
  and a3 (a0_out[3], a[3], not_1_out);
  and a4 (a0_out[4], a[4], not_1_out);
  and a5 (a0_out[5], a[5], not_1_out);
  and a6 (a0_out[6], a[6], not_1_out);
  and a7 (a0_out[7], a[7], not_1_out);
  and a8 (a0_out[8], a[8], not_1_out);
  and a9 (a0_out[9], a[9], not_1_out);
  and a10 (a0_out[10], a[10], not_1_out);
  and a11 (a0_out[11], a[11], not_1_out);
  and a12 (a0_out[12], a[12], not_1_out);
  and a13 (a0_out[13], a[13], not_1_out);
  and a14 (a0_out[14], a[14], not_1_out);
  and a15 (a0_out[15], a[15], not_1_out);
  assign and_1_out = b & bit_extender_2_out;  // AND_Gate and_1, 16 bits wide
  assign and_2_out = c & bit_extender_1_out;  // AND_Gate and_2, 16 bits wide
  assign and_3_out = d & bit_extender_2_out;  // AND_Gate and_3, 16 bits wide
  assign or_1_out = a0_out | and_1_out;  // OR_Gate or_1, 16 bits wide
  assign or_2_out = and_2_out | and_3_out;  // OR_Gate or_2, 16 bits wide
  assign and_4_out = or_1_out & bit_extender_3_out;  // AND_Gate and_4, 16 bits wide
  assign and_5_out = or_2_out & bit_extender_4_out;  // AND_Gate and_5, 16 bits wide
  assign out = and_4_out | and_5_out;  // OR_Gate or_3, 16 bits wide

  // Notes on the sheet:
  //   copies 1 bit input across 16 outputs
  //   16 individual AND gates
  //   16-bit ANDs
  //   16-bit ORs
endmodule

module _8_WAY_MUX_16 (
  input  [15:0] a,
  input  [15:0] b,
  input  [15:0] c,
  input  [15:0] d,
  input  [15:0] e,
  input  [15:0] f,
  input  [15:0] g,
  input  [15:0] h,
  input  sel_0,
  input  sel_1,
  input  sel_2,
  output [15:0] out
);

  wire not_1_out, not_2_out, not_3_out;
  wire [15:0] and_1_out, and_2_out, and_3_out, and_4_out, and_5_out, and_6_out, and_7_out, and_8_out,
       and_9_out, and_10_out, and_11_out, and_12_out, and_13_out, and_14_out, bit_extender_1_out,
       bit_extender_2_out, bit_extender_3_out, bit_extender_4_out, bit_extender_5_out, bit_extender_6_out,
       or_1_out, or_2_out, or_3_out, or_4_out, or_5_out, or_6_out;

  assign bit_extender_1_out = {{15{sel_0}}, sel_0};  // Bit_Extender bit_extender_1
  not not_1 (not_1_out, sel_0);
  assign bit_extender_2_out = {{15{not_1_out}}, not_1_out};  // Bit_Extender bit_extender_2
  assign bit_extender_3_out = {{15{sel_1}}, sel_1};  // Bit_Extender bit_extender_3
  assign bit_extender_4_out = {{15{not_2_out}}, not_2_out};  // Bit_Extender bit_extender_4
  not not_2 (not_2_out, sel_1);
  assign bit_extender_5_out = {{15{sel_2}}, sel_2};  // Bit_Extender bit_extender_5
  not not_3 (not_3_out, sel_2);
  assign bit_extender_6_out = {{15{not_3_out}}, not_3_out};  // Bit_Extender bit_extender_6
  assign and_1_out = a & bit_extender_2_out;  // AND_Gate and_1, 16 bits wide
  assign or_1_out = and_1_out | and_2_out;  // OR_Gate or_1, 16 bits wide
  assign and_2_out = b & bit_extender_1_out;  // AND_Gate and_2, 16 bits wide
  assign and_3_out = c & bit_extender_2_out;  // AND_Gate and_3, 16 bits wide
  assign or_2_out = and_3_out | and_4_out;  // OR_Gate or_2, 16 bits wide
  assign and_4_out = d & bit_extender_1_out;  // AND_Gate and_4, 16 bits wide
  assign and_5_out = e & bit_extender_2_out;  // AND_Gate and_5, 16 bits wide
  assign or_3_out = and_5_out | and_6_out;  // OR_Gate or_3, 16 bits wide
  assign and_6_out = f & bit_extender_1_out;  // AND_Gate and_6, 16 bits wide
  assign and_7_out = g & bit_extender_2_out;  // AND_Gate and_7, 16 bits wide
  assign or_4_out = and_7_out | and_8_out;  // OR_Gate or_4, 16 bits wide
  assign and_8_out = h & bit_extender_1_out;  // AND_Gate and_8, 16 bits wide
  assign and_9_out = or_1_out & bit_extender_4_out;  // AND_Gate and_9, 16 bits wide
  assign or_5_out = and_9_out | and_10_out;  // OR_Gate or_5, 16 bits wide
  assign and_10_out = or_2_out & bit_extender_3_out;  // AND_Gate and_10, 16 bits wide
  assign and_11_out = or_3_out & bit_extender_4_out;  // AND_Gate and_11, 16 bits wide
  assign or_6_out = and_11_out | and_12_out;  // OR_Gate or_6, 16 bits wide
  assign and_12_out = or_4_out & bit_extender_3_out;  // AND_Gate and_12, 16 bits wide
  assign and_13_out = or_5_out & bit_extender_6_out;  // AND_Gate and_13, 16 bits wide
  assign out = and_13_out | and_14_out;  // OR_Gate or_7, 16 bits wide
  assign and_14_out = or_6_out & bit_extender_5_out;  // AND_Gate and_14, 16 bits wide
endmodule

module _4_WAY_DMUX (
  input  in,
  input  sel_0,
  input  sel_1,
  output a,
  output b,
  output c,
  output d
);

  wire and_1_out, and_2_out, and_3_out, and_4_out, not_1_out, not_2_out;

  not not_1 (not_1_out, sel_0);
  not not_2 (not_2_out, sel_1);
  and and_1 (and_1_out, not_1_out, not_2_out);
  and and_2 (and_2_out, sel_0, not_2_out);
  and and_3 (and_3_out, sel_1, not_1_out);
  and and_4 (and_4_out, sel_1, sel_0);
  and and_5 (a, in, and_1_out);
  and and_6 (b, in, and_2_out);
  and and_7 (c, in, and_3_out);
  and and_8 (d, in, and_4_out);
endmodule

module _8_WAY_DMUX (
  input  in,
  input  sel_0,
  input  sel_1,
  input  sel_2,
  output a,
  output b,
  output c,
  output d,
  output a_2,
  output b_2,
  output c_2,
  output d_2
);

  wire and_1_out, and_2_out, and_3_out, and_4_out, and_5_out, and_6_out, and_7_out, and_8_out, and_9_out,
       and_10_out, and_11_out, and_12_out, not_1_out, not_2_out, not_3_out;

  not not_1 (not_1_out, sel_0);
  not not_2 (not_2_out, sel_1);
  not not_3 (not_3_out, sel_2);
  and and_1 (and_1_out, not_1_out, not_2_out);
  and and_2 (and_2_out, sel_0, not_2_out);
  and and_3 (and_3_out, sel_1, not_1_out);
  and and_4 (and_4_out, sel_1, sel_0);
  and and_5 (and_5_out, and_1_out, not_3_out);
  and and_6 (and_6_out, and_2_out, not_3_out);
  and and_7 (and_7_out, and_3_out, not_3_out);
  and and_8 (and_8_out, and_4_out, not_3_out);
  and and_9 (and_9_out, and_1_out, sel_2);
  and and_10 (and_10_out, and_2_out, sel_2);
  and and_11 (and_11_out, and_3_out, sel_2);
  and and_12 (and_12_out, and_4_out, sel_2);
  and and_13 (a, in, and_5_out);
  and and_14 (b, in, and_6_out);
  and and_15 (c, in, and_7_out);
  and and_16 (d, in, and_8_out);
  and and_17 (a_2, in, and_9_out);
  and and_18 (b_2, in, and_10_out);
  and and_19 (c_2, in, and_11_out);
  and and_20 (d_2, in, and_12_out);
endmodule
