// Logisim project chapter2.circ as structural Verilog: 5 circuits, main circuit half-adder
module half_adder (
  input  a,
  input  b,
  output sum,
  output carry
);

  xor xor_1 (sum, a, b);
  and and_1 (carry, a, b);
endmodule

module full_adder (
  input  a,
  input  b,
  input  c,
  output sum,
  output carry
);

  wire half_adder_1_carry, half_adder_1_sum, half_adder_2_carry;

  half_adder half_adder_1 (.a(a), .b(b), .sum(half_adder_1_sum), .carry(half_adder_1_carry));
  half_adder half_adder_2 (.a(c), .b(half_adder_1_sum), .sum(sum), .carry(half_adder_2_carry));
  or or_1 (carry, half_adder_2_carry, half_adder_1_carry);
endmodule

module _16_bit_adder (
  input  [15:0] b,
  input  [15:0] a,
  output [15:0] out_3
);

  wire full_adder_1_carry, full_adder_2_carry, full_adder_3_carry, full_adder_4_carry, full_adder_5_carry,
       full_adder_6_carry, full_adder_7_carry, full_adder_8_carry, full_adder_9_carry, full_adder_10_carry,
       full_adder_11_carry, full_adder_12_carry, full_adder_13_carry, full_adder_14_carry,
       full_adder_15_carry;

  full_adder full_adder_1 (.a(a[0]), .b(b[0]), .c(1'b0), .sum(out_3[0]), .carry(full_adder_1_carry));
  full_adder full_adder_2 (.a(a[1]), .b(b[1]), .c(full_adder_1_carry), .sum(out_3[1]), .carry(full_adder_2_carry));
  full_adder full_adder_3 (.a(a[2]), .b(b[2]), .c(full_adder_2_carry), .sum(out_3[2]), .carry(full_adder_3_carry));
  full_adder full_adder_4 (.a(a[3]), .b(b[3]), .c(full_adder_3_carry), .sum(out_3[3]), .carry(full_adder_4_carry));
  full_adder full_adder_5 (.a(a[4]), .b(b[4]), .c(full_adder_4_carry), .sum(out_3[4]), .carry(full_adder_5_carry));
  full_adder full_adder_6 (.a(a[5]), .b(b[5]), .c(full_adder_5_carry), .sum(out_3[5]), .carry(full_adder_6_carry));
  full_adder full_adder_7 (.a(a[6]), .b(b[6]), .c(full_adder_6_carry), .sum(out_3[6]), .carry(full_adder_7_carry));
  full_adder full_adder_8 (.a(a[7]), .b(b[7]), .c(full_adder_7_carry), .sum(out_3[7]), .carry(full_adder_8_carry));
  full_adder full_adder_9 (.a(a[8]), .b(b[8]), .c(full_adder_8_carry), .sum(out_3[8]), .carry(full_adder_9_carry));
  full_adder full_adder_10 (.a(a[9]), .b(b[9]), .c(full_adder_9_carry), .sum(out_3[9]), .carry(full_adder_10_carry));
  full_adder full_adder_11 (
    .a(a[10]), .b(b[10]), .c(full_adder_10_carry), .sum(out_3[10]), .carry(full_adder_11_carry));
  full_adder full_adder_12 (
    .a(a[11]), .b(b[11]), .c(full_adder_11_carry), .sum(out_3[11]), .carry(full_adder_12_carry));
  full_adder full_adder_13 (
    .a(a[12]), .b(b[12]), .c(full_adder_12_carry), .sum(out_3[12]), .carry(full_adder_13_carry));
  full_adder full_adder_14 (
    .a(a[13]), .b(b[13]), .c(full_adder_13_carry), .sum(out_3[13]), .carry(full_adder_14_carry));
  full_adder full_adder_15 (
    .a(a[14]), .b(b[14]), .c(full_adder_14_carry), .sum(out_3[14]), .carry(full_adder_15_carry));
  full_adder full_adder_16 (.a(a[15]), .b(b[15]), .c(full_adder_15_carry), .sum(out_3[15]));  // open: carry
endmodule

module _16_bit_incrementer (
  input  [15:0] b,
  input  [15:0] a,
  output [15:0] out_3
);

  wire full_adder_1_carry, full_adder_2_carry, full_adder_3_carry, full_adder_4_carry, full_adder_5_carry,
       full_adder_6_carry, full_adder_7_carry, full_adder_8_carry, full_adder_9_carry, full_adder_10_carry,
       full_adder_11_carry, full_adder_12_carry, full_adder_13_carry, full_adder_14_carry,
       full_adder_15_carry;

  full_adder full_adder_1 (.a(a[0]), .b(b[0]), .c(1'b0), .sum(out_3[0]), .carry(full_adder_1_carry));
  full_adder full_adder_2 (.a(a[1]), .b(b[1]), .c(full_adder_1_carry), .sum(out_3[1]), .carry(full_adder_2_carry));
  full_adder full_adder_3 (.a(a[2]), .b(b[2]), .c(full_adder_2_carry), .sum(out_3[2]), .carry(full_adder_3_carry));
  full_adder full_adder_4 (.a(a[3]), .b(b[3]), .c(full_adder_3_carry), .sum(out_3[3]), .carry(full_adder_4_carry));
  full_adder full_adder_5 (.a(a[4]), .b(b[4]), .c(full_adder_4_carry), .sum(out_3[4]), .carry(full_adder_5_carry));
  full_adder full_adder_6 (.a(a[5]), .b(b[5]), .c(full_adder_5_carry), .sum(out_3[5]), .carry(full_adder_6_carry));
  full_adder full_adder_7 (.a(a[6]), .b(b[6]), .c(full_adder_6_carry), .sum(out_3[6]), .carry(full_adder_7_carry));
  full_adder full_adder_8 (.a(a[7]), .b(b[7]), .c(full_adder_7_carry), .sum(out_3[7]), .carry(full_adder_8_carry));
  full_adder full_adder_9 (.a(a[8]), .b(b[8]), .c(full_adder_8_carry), .sum(out_3[8]), .carry(full_adder_9_carry));
  full_adder full_adder_10 (.a(a[9]), .b(b[9]), .c(full_adder_9_carry), .sum(out_3[9]), .carry(full_adder_10_carry));
  full_adder full_adder_11 (
    .a(a[10]), .b(b[10]), .c(full_adder_10_carry), .sum(out_3[10]), .carry(full_adder_11_carry));
  full_adder full_adder_12 (
    .a(a[11]), .b(b[11]), .c(full_adder_11_carry), .sum(out_3[11]), .carry(full_adder_12_carry));
  full_adder full_adder_13 (
    .a(a[12]), .b(b[12]), .c(full_adder_12_carry), .sum(out_3[12]), .carry(full_adder_13_carry));
  full_adder full_adder_14 (
    .a(a[13]), .b(b[13]), .c(full_adder_13_carry), .sum(out_3[13]), .carry(full_adder_14_carry));
  full_adder full_adder_15 (
    .a(a[14]), .b(b[14]), .c(full_adder_14_carry), .sum(out_3[14]), .carry(full_adder_15_carry));
  full_adder full_adder_16 (.a(a[15]), .b(b[15]), .c(full_adder_15_carry), .sum(out_3[15]));  // open: carry
endmodule

module alu (
  input  zx,
  input  nx,
  input  zy,
  input  ny,
  input  f,
  input  no,
  input  [15:0] x,
  input  [15:0] y,
  output [15:0] out,
  output ng,
  output zr
);

  wire or_1_out;
  wire [15:0] adder_1_out, and_1_out, multiplexer_1_out, multiplexer_2_out, multiplexer_3_out,
       multiplexer_4_out, multiplexer_5_out, not_1_out, not_2_out, not_3_out;

  // Probe on x
  // Probe on y
  Multiplexer #(.width(16), .enable("false")) multiplexer_1 (
    .in0(x), .in1({16{1'b0}}), .out(multiplexer_1_out), .sel(zx));
  Multiplexer #(.width(16), .enable("false")) multiplexer_2 (
    .in0(y), .in1({16{1'b0}}), .out(multiplexer_2_out), .sel(zy));
  assign not_1_out = ~multiplexer_1_out;  // NOT_Gate not_1, 16 bits wide
  assign not_2_out = ~multiplexer_2_out;  // NOT_Gate not_2, 16 bits wide
  // Probe on multiplexer_3_out
  Multiplexer #(.width(16), .enable("false")) multiplexer_3 (
    .in0(multiplexer_1_out), .in1(not_1_out), .out(multiplexer_3_out), .sel(nx));
  Multiplexer #(.width(16), .enable("false")) multiplexer_4 (
    .in0(multiplexer_2_out), .in1(not_2_out), .out(multiplexer_4_out), .sel(ny));
  assign and_1_out = multiplexer_3_out & multiplexer_4_out;  // AND_Gate and_1, 16 bits wide
  Adder #(.width(16)) adder_1 (.a(multiplexer_3_out), .b(multiplexer_4_out), .out(adder_1_out));  // open: cin, cout
  // Probe on multiplexer_4_out
  Multiplexer #(.width(16), .enable("false")) multiplexer_5 (
    .in0(and_1_out), .in1(adder_1_out), .out(multiplexer_5_out), .sel(f));
  assign not_3_out = ~multiplexer_5_out;  // NOT_Gate not_3, 16 bits wide
  // Probe on {ng, out[14:0]}
  Multiplexer #(.width(16), .enable("false")) multiplexer_6 (
    .in0(multiplexer_5_out), .in1(not_3_out), .out({ng, out[14:0]}), .sel(no));
  or or_1 (or_1_out, ng, out[14], out[13], out[12], out[11], out[10], out[9], out[8], out[7], out[6], out[5], out[4], out[3], out[2], out[1], out[0]);
  not not_4 (zr, or_1_out);

  assign out[15] = ng;
endmodule
