// Logisim project chapter3.circ as structural Verilog: 4 circuits, main circuit bit
module \bit  (
  input  load,
  input  clock,
  input  in,
  output out
);

  wire multiplexer_1_out;

  Multiplexer #(.enable("false")) multiplexer_1 (.in0(out), .in1(in), .out(multiplexer_1_out), .sel(load));
  D_Flip_Flop d_ff_1 (.clk(clock), .D(multiplexer_1_out), .Q(out));  // open: Qn, preset, en, reset
endmodule

module register (
  input  clock,
  input  load,
  input  [15:0] in,
  output [15:0] out
);

  \bit  bit_1 (.in(in[0]), .load(load), .clock(clock), .out(out[0]));
  \bit  bit_2 (.in(in[1]), .load(load), .clock(clock), .out(out[1]));
  \bit  bit_3 (.in(in[2]), .load(load), .clock(clock), .out(out[2]));
  \bit  bit_4 (.in(in[3]), .load(load), .clock(clock), .out(out[3]));
  \bit  bit_5 (.in(in[4]), .load(load), .clock(clock), .out(out[4]));
  \bit  bit_6 (.in(in[5]), .load(load), .clock(clock), .out(out[5]));
  \bit  bit_7 (.in(in[6]), .load(load), .clock(clock), .out(out[6]));
  \bit  bit_8 (.in(in[7]), .load(load), .clock(clock), .out(out[7]));
  \bit  bit_9 (.in(in[8]), .load(load), .clock(clock), .out(out[8]));
  \bit  bit_10 (.in(in[9]), .load(load), .clock(clock), .out(out[9]));
  \bit  bit_11 (.in(in[10]), .load(load), .clock(clock), .out(out[10]));
  \bit  bit_12 (.in(in[11]), .load(load), .clock(clock), .out(out[11]));
  \bit  bit_13 (.in(in[12]), .load(load), .clock(clock), .out(out[12]));
  \bit  bit_14 (.in(in[13]), .load(load), .clock(clock), .out(out[13]));
  \bit  bit_15 (.in(in[14]), .load(load), .clock(clock), .out(out[14]));
  \bit  bit_16 (.in(in[15]), .load(load), .clock(clock), .out(out[15]));
endmodule

module ram8 (
  input  load,
  input  clock,
  input  [15:0] in,
  input  [2:0] address,
  output [15:0] out
);

  wire clock_1_out, demultiplexer_1_out0, demultiplexer_1_out1, demultiplexer_1_out2, demultiplexer_1_out3,
       demultiplexer_1_out4, demultiplexer_1_out5, demultiplexer_1_out6, demultiplexer_1_out7;
  wire [15:0] demultiplexer_2_out0, demultiplexer_2_out1, demultiplexer_2_out2, demultiplexer_2_out3,
       demultiplexer_2_out4, demultiplexer_2_out5, demultiplexer_2_out6, demultiplexer_2_out7,
       register_1_out, register_2_out, register_3_out, register_4_out, register_5_out, register_6_out,
       register_7_out, register_8_out;

  Demultiplexer #(.select(3), .enable("false")) demultiplexer_1 (
    .out0(demultiplexer_1_out0), .out1(demultiplexer_1_out1), .out2(demultiplexer_1_out2),
    .out3(demultiplexer_1_out3), .out4(demultiplexer_1_out4), .out5(demultiplexer_1_out5),
    .out6(demultiplexer_1_out6), .out7(demultiplexer_1_out7), .in(load), .sel(address));
  Clock clock_1 (.out(clock_1_out));
  Demultiplexer #(.select(3), .width(16), .enable("false")) demultiplexer_2 (
    .out0(demultiplexer_2_out0), .out1(demultiplexer_2_out1), .out2(demultiplexer_2_out2),
    .out3(demultiplexer_2_out3), .out4(demultiplexer_2_out4), .out5(demultiplexer_2_out5),
    .out6(demultiplexer_2_out6), .out7(demultiplexer_2_out7), .in(in), .sel(address));
  register register_1 (
    .clock(clock_1_out), .load(demultiplexer_1_out0), .in(demultiplexer_2_out0), .out(register_1_out));
  register register_2 (
    .clock(clock_1_out), .load(demultiplexer_1_out1), .in(demultiplexer_2_out1), .out(register_2_out));
  register register_3 (
    .clock(clock_1_out), .load(demultiplexer_1_out2), .in(demultiplexer_2_out2), .out(register_3_out));
  register register_4 (
    .clock(clock_1_out), .load(demultiplexer_1_out3), .in(demultiplexer_2_out3), .out(register_4_out));
  register register_5 (
    .clock(clock_1_out), .load(demultiplexer_1_out4), .in(demultiplexer_2_out4), .out(register_5_out));
  register register_6 (
    .clock(clock_1_out), .load(demultiplexer_1_out5), .in(demultiplexer_2_out5), .out(register_6_out));
  register register_7 (
    .clock(clock_1_out), .load(demultiplexer_1_out6), .in(demultiplexer_2_out6), .out(register_7_out));
  register register_8 (
    .clock(clock_1_out), .load(demultiplexer_1_out7), .in(demultiplexer_2_out7), .out(register_8_out));
  Multiplexer #(.select(3), .width(16), .enable("false")) multiplexer_1 (
    .in0(register_1_out), .in1(register_2_out), .in2(register_3_out), .in3(register_4_out),
    .in4(register_5_out), .in5(register_6_out), .in6(register_7_out), .in7(register_8_out), .out(out),
    .sel(address));
endmodule

module counter (
  input  clock,
  input  [15:0] in,
  input  [15:0] in_2,
  input  inc,
  input  load,
  input  reset,
  input  [15:0] zero,
  output [15:0] out
);

  wire clock_1_out;
  wire [15:0] adder_1_out, multiplexer_1_out, multiplexer_2_out, multiplexer_3_out;

  Adder #(.width(16)) adder_1 (.a(out), .b(in), .out(adder_1_out));  // open: cin, cout
  // Probe on multiplexer_1_out
  Multiplexer #(.width(16), .enable("false")) multiplexer_1 (
    .in0(out), .in1(adder_1_out), .out(multiplexer_1_out), .sel(inc));
  // Probe on multiplexer_3_out
  // Probe on multiplexer_2_out
  Multiplexer #(.width(16), .enable("false")) multiplexer_2 (
    .in0(multiplexer_1_out), .in1(in_2), .out(multiplexer_2_out), .sel(load));
  Clock clock_1 (.out(clock_1_out));
  Multiplexer #(.width(16), .enable("false")) multiplexer_3 (
    .in0(multiplexer_2_out), .in1(zero), .out(multiplexer_3_out), .sel(reset));
  \bit  bit_1 (.in(multiplexer_3_out[0]), .load(1'b1), .clock(clock_1_out), .out(out[0]));
  \bit  bit_2 (.in(multiplexer_3_out[1]), .load(1'b1), .clock(clock_1_out), .out(out[1]));
  \bit  bit_3 (.in(multiplexer_3_out[2]), .load(1'b1), .clock(clock_1_out), .out(out[2]));
  \bit  bit_4 (.in(multiplexer_3_out[3]), .load(1'b1), .clock(clock_1_out), .out(out[3]));
  \bit  bit_5 (.in(multiplexer_3_out[4]), .load(1'b1), .clock(clock_1_out), .out(out[4]));
  \bit  bit_6 (.in(multiplexer_3_out[5]), .load(1'b1), .clock(clock_1_out), .out(out[5]));
  \bit  bit_7 (.in(multiplexer_3_out[6]), .load(1'b1), .clock(clock_1_out), .out(out[6]));
  \bit  bit_8 (.in(multiplexer_3_out[7]), .load(1'b1), .clock(clock_1_out), .out(out[7]));
  \bit  bit_9 (.in(multiplexer_3_out[8]), .load(1'b1), .clock(clock_1_out), .out(out[8]));
  \bit  bit_10 (.in(multiplexer_3_out[9]), .load(1'b1), .clock(clock_1_out), .out(out[9]));
  \bit  bit_11 (.in(multiplexer_3_out[10]), .load(1'b1), .clock(clock_1_out), .out(out[10]));
  \bit  bit_12 (.in(multiplexer_3_out[11]), .load(1'b1), .clock(clock_1_out), .out(out[11]));
  \bit  bit_13 (.in(multiplexer_3_out[12]), .load(1'b1), .clock(clock_1_out), .out(out[12]));
  \bit  bit_14 (.in(multiplexer_3_out[13]), .load(1'b1), .clock(clock_1_out), .out(out[13]));
  \bit  bit_15 (.in(multiplexer_3_out[14]), .load(1'b1), .clock(clock_1_out), .out(out[14]));
  \bit  bit_16 (.in(multiplexer_3_out[15]), .load(1'b1), .clock(clock_1_out), .out(out[15]));
endmodule
