// Logisim project chapter5.circ as structural Verilog: 5 circuits, main circuit alu
module cpu (
  input  [15:0] instruction,
  input  [15:0] inM,
  input  reset,
  output [15:0] outM,
  output writeM,
  output [15:0] addressM,
  output [15:0] pc
);

  wire and_1_out, and_2_out, clock, decoder_1_out1, decoder_1_out2, decoder_1_out3, decoder_1_out4,
       decoder_1_out5, decoder_1_out6, decoder_1_out7, decoder_2_out1, decoder_2_out2, decoder_2_out3,
       decoder_2_out4, decoder_2_out5, decoder_2_out6, decoder_2_out7, JEQ_out, JGE_out, JGT_out, JLE_out,
       JLT_out, JMP_out, JNE_out, ng, not_1_out, not_2_out, or_1_out, or_2_out, or_3_out, or_4_out, or_5_out,
       zr;
  wire [15:0] D_q, multiplexer_1_out, multiplexer_2_out;

  Clock clock_1 (.out(clock));
  Decoder #(.select(3), .enable("false")) decoder_1 (
    .out1(decoder_1_out1), .out2(decoder_1_out2), .out3(decoder_1_out3), .out4(decoder_1_out4),
    .out5(decoder_1_out5), .out6(decoder_1_out6), .out7(decoder_1_out7), .sel(instruction[2:0]));  // open: out0
  // Probe on instruction
  not not_1 (not_1_out, zr);
  not not_2 (not_2_out, ng);
  and and_1 (and_1_out, not_2_out, not_1_out);
  or or_1 (or_1_out, zr, not_2_out);
  and and_2 (and_2_out, ng, not_1_out);
  or or_2 (or_2_out, ng, zr);
  // Probe on multiplexer_1_out
  Multiplexer #(.width(16), .enable("false")) multiplexer_1 (
    .in0(outM), .in1(instruction), .out(multiplexer_1_out), .sel(instruction[15]));
  or or_3 (or_3_out, decoder_2_out7, decoder_2_out6, decoder_2_out4, decoder_2_out5);
  and JGT (JGT_out, decoder_1_out1, and_1_out);
  and JEQ (JEQ_out, decoder_1_out2, zr);
  and JGE (JGE_out, decoder_1_out3, or_1_out);
  and JLT (JLT_out, decoder_1_out4, and_2_out);
  and JNE (JNE_out, decoder_1_out5, not_1_out);
  and JLE (JLE_out, decoder_1_out6, or_2_out);
  and JMP (JMP_out, decoder_1_out7, decoder_1_out7);
  or or_4 (or_4_out, decoder_2_out7, decoder_2_out2, decoder_2_out6, decoder_2_out3);
  Register #(.width(16)) A (.D(multiplexer_1_out), .en(or_3_out), .Q(addressM), .clk(clock));  // open: clr
  or or_5 (or_5_out, JGT_out, JEQ_out, JGE_out, JLT_out, JNE_out, JLE_out, JMP_out);
  // Probe on D_q
  Register #(.width(16)) D (.D(outM), .en(or_4_out), .Q(D_q), .clk(clock));  // open: clr
  Multiplexer #(.width(16), .enable("false")) multiplexer_2 (
    .in0(addressM), .in1(inM), .out(multiplexer_2_out), .sel(instruction[12]));
  // Probe on addressM
  Counter #(.width(16), .max('hffff)) u_PC (
    .load(or_5_out), .D(addressM), .Q(pc), .clk(clock), .clr(reset));  // open: count, carry
  alu alu_1 (
    .x(D_q), .y(multiplexer_2_out), .zx(instruction[11]), .nx(instruction[10]), .zy(instruction[9]),
    .ny(instruction[8]), .f(instruction[7]), .no(instruction[6]), .ng(ng), .zr(zr), .out(outM));
  Decoder #(.select(3), .enable("false")) decoder_2 (
    .out1(decoder_2_out1), .out2(decoder_2_out2), .out3(decoder_2_out3), .out4(decoder_2_out4),
    .out5(decoder_2_out5), .out6(decoder_2_out6), .out7(decoder_2_out7), .sel(instruction[5:3]));  // open: out0
  // Probe on outM
  // Probe on addressM
  // Probe on pc
  or or_6 (writeM, decoder_2_out1, decoder_2_out7, decoder_2_out5, decoder_2_out3);

  // Other names for the same wires on the sheet: _0_t_t = instruction[0]; _0_t = instruction[1]; _0 = instruction[2];
  //   d3 = instruction[3]; d2 = instruction[4]; d1 = instruction[5]; no = instruction[6]; f = instruction[7];
  //   ny = instruction[8]; zy = instruction[9]; nx = instruction[10]; zx = instruction[11]; a = instruction[12]

  // Notes on the sheet:
  //   j
  //   d
  //   c
  //   a
  //   x
  //   i
endmodule

module alu (
  input  zx,
  input  nx,
  input  zy,
  input  ny,
  input  f,
  input  no,
  input  [15:0] x,
  input  [15:0] y,
  output [15:0] out,
  output ng,
  output zr
);

  wire or_1_out;
  wire [15:0] adder_1_out, and_1_out, multiplexer_1_out, multiplexer_2_out, multiplexer_3_out,
       multiplexer_4_out, multiplexer_5_out, not_1_out, not_2_out, not_3_out;

  // Probe on x
  // Probe on y
  Multiplexer #(.width(16), .enable("false")) multiplexer_1 (
    .in0(x), .in1({16{1'b0}}), .out(multiplexer_1_out), .sel(zx));
  Multiplexer #(.width(16), .enable("false")) multiplexer_2 (
    .in0(y), .in1({16{1'b0}}), .out(multiplexer_2_out), .sel(zy));
  assign not_1_out = ~multiplexer_1_out;  // NOT_Gate not_1, 16 bits wide
  assign not_2_out = ~multiplexer_2_out;  // NOT_Gate not_2, 16 bits wide
  // Probe on multiplexer_3_out
  Multiplexer #(.width(16), .enable("false")) multiplexer_3 (
    .in0(multiplexer_1_out), .in1(not_1_out), .out(multiplexer_3_out), .sel(nx));
  Multiplexer #(.width(16), .enable("false")) multiplexer_4 (
    .in0(multiplexer_2_out), .in1(not_2_out), .out(multiplexer_4_out), .sel(ny));
  assign and_1_out = multiplexer_3_out & multiplexer_4_out;  // AND_Gate and_1, 16 bits wide
  Adder #(.width(16)) adder_1 (.a(multiplexer_3_out), .b(multiplexer_4_out), .out(adder_1_out));  // open: cin, cout
  // Probe on multiplexer_4_out
  Multiplexer #(.width(16), .enable("false")) multiplexer_5 (
    .in0(and_1_out), .in1(adder_1_out), .out(multiplexer_5_out), .sel(f));
  assign not_3_out = ~multiplexer_5_out;  // NOT_Gate not_3, 16 bits wide
  // Probe on {ng, out[14:0]}
  Multiplexer #(.width(16), .enable("false")) multiplexer_6 (
    .in0(multiplexer_5_out), .in1(not_3_out), .out({ng, out[14:0]}), .sel(no));
  or or_1 (or_1_out, ng, out[14], out[13], out[12], out[11], out[10], out[9], out[8], out[7], out[6], out[5], out[4], out[3], out[2], out[1], out[0]);
  not not_4 (zr, or_1_out);

  assign out[15] = ng;
endmodule

module data_memory (
);

  RAM #(.addrWidth(16), .dataWidth(16)) ram_1 ();  // open: addr, data, sel, clk, ld, clr
endmodule

module computer (
);

  wire cpu_1_writem;
  wire [15:0] cpu_1_addressm, cpu_1_outm, cpu_1_pc, ram_1_data, rom_1_data;

  ROM #(.addrWidth(16), .dataWidth(16)) rom_1 (.addr(cpu_1_pc), .data(rom_1_data));  // open: sel
  cpu cpu_1 (
    .instruction(rom_1_data), .inM(ram_1_data), .outM(cpu_1_outm), .writeM(cpu_1_writem),
    .addressM(cpu_1_addressm), .pc(cpu_1_pc));  // open: reset
  RAM #(.addrWidth(16), .dataWidth(16), .bus("separate")) ram_1 (
    .addr(cpu_1_addressm), .din(cpu_1_outm), .data(ram_1_data), .str(cpu_1_writem), .ld(1'b1));  // open: sel, clk, clr
endmodule

module compfull (
  input  reset
);

  wire _0, _0_t, _0_t_t, a, and_1_out, and_2_out, and_3_out, clock, d1, d2, d3, decoder_1_out1,
       decoder_1_out2, decoder_1_out3, decoder_1_out4, decoder_1_out5, decoder_1_out6, decoder_1_out7,
       decoder_2_out1, decoder_2_out2, decoder_2_out3, decoder_2_out4, decoder_2_out5, decoder_2_out6,
       decoder_2_out7, f, JEQ_out, JGE_out, JGT_out, JLE_out, JLT_out, JMP_out, JNE_out, ng, no, not_1_out,
       not_2_out, not_3_out, nx, ny, or_1_out, or_2_out, or_3_out, or_4_out, or_5_out, or_6_out, writeM, zr,
       zx, zy;
  wire [15:0] addressM, D_q, inM, multiplexer_1_out, multiplexer_2_out, outM, pc;
  wire [15:13] rom_1_data;

  // Probe on outM
  RAM #(.addrWidth(16), .dataWidth(16), .bus("separate")) ram_1 (
    .addr(addressM), .din(outM), .data(inM), .str(writeM), .clk(clock), .ld(1'b1));  // open: sel, clr
  Clock clock_1 (.out(clock));
  ROM #(.addrWidth(16), .dataWidth(16)) rom_1 (
    .addr(pc), .data({rom_1_data, a, zx, nx, zy, ny, f, no, d1, d2, d3, _0, _0_t, _0_t_t}));  // open: sel
  // Probe on inM
  Decoder #(.select(3), .enable("false")) decoder_1 (
    .out1(decoder_1_out1), .out2(decoder_1_out2), .out3(decoder_1_out3), .out4(decoder_1_out4),
    .out5(decoder_1_out5), .out6(decoder_1_out6), .out7(decoder_1_out7), .sel({_0, _0_t, _0_t_t}));  // open: out0
  // Probe on {rom_1_data, a, zx, nx, zy, ny, f, no, d1, d2, d3, _0, _0_t, _0_t_t}
  not not_1 (not_1_out, ng);
  not not_2 (not_2_out, zr);
  Multiplexer #(.width(16), .enable("false")) multiplexer_1 (
    .in0({rom_1_data, a, zx, nx, zy, ny, f, no, d1, d2, d3, _0, _0_t, _0_t_t}), .in1(outM),
    .out(multiplexer_1_out), .sel(rom_1_data[15]));
  or or_1 (or_1_out, decoder_2_out7, decoder_2_out6, decoder_2_out4, decoder_2_out5);
  not not_3 (not_3_out, rom_1_data[15]);
  and and_1 (and_1_out, not_1_out, not_2_out);
  or or_2 (or_2_out, zr, not_1_out);
  and and_2 (and_2_out, ng, not_2_out);
  or or_3 (or_3_out, ng, zr);
  or or_4 (or_4_out, decoder_2_out7, decoder_2_out2, decoder_2_out6, decoder_2_out3);
  // Probe on multiplexer_1_out
  Register #(.width(16)) u_A (.D(multiplexer_1_out), .en(or_5_out), .Q(addressM), .clk(clock));  // open: clr
  or or_5 (or_5_out, or_1_out, not_3_out);
  and JGT (JGT_out, decoder_1_out1, and_1_out);
  and JEQ (JEQ_out, decoder_1_out2, zr);
  and JGE (JGE_out, decoder_1_out3, or_2_out);
  and JLT (JLT_out, decoder_1_out4, and_2_out);
  and JNE (JNE_out, decoder_1_out5, not_2_out);
  and JLE (JLE_out, decoder_1_out6, or_3_out);
  and JMP (JMP_out, decoder_1_out7, decoder_1_out7);
  // Probe on addressM
  and and_3 (and_3_out, rom_1_data[15], or_6_out);
  or or_6 (or_6_out, JGT_out, JEQ_out, JGE_out, JLT_out, JNE_out, JLE_out, JMP_out);
  // Probe on D_q
  Register #(.width(16)) D (.D(outM), .en(or_4_out), .Q(D_q), .clk(clock));  // open: clr
  Multiplexer #(.width(16), .enable("false")) multiplexer_2 (
    .in0(addressM), .in1(inM), .out(multiplexer_2_out), .sel(a));
  // Probe on multiplexer_2_out
  Counter #(.width(16), .max('hffff)) u_PC (
    .load(and_3_out), .D(addressM), .Q(pc), .clk(clock), .clr(reset));  // open: count, carry
  alu alu_1 (
    .x(D_q), .y(multiplexer_2_out), .zx(zx), .nx(nx), .zy(zy), .ny(ny), .f(f), .no(no), .ng(ng), .zr(zr),
    .out(outM));
  // Probe on outM
  // Probe on addressM
  // Probe on pc
  Decoder #(.select(3), .enable("false")) decoder_2 (
    .out1(decoder_2_out1), .out2(decoder_2_out2), .out3(decoder_2_out3), .out4(decoder_2_out4),
    .out5(decoder_2_out5), .out6(decoder_2_out6), .out7(decoder_2_out7), .sel({d1, d2, d3}));  // open: out0
  // Probe on outM
  or or_7 (writeM, decoder_2_out1, decoder_2_out7, decoder_2_out5, decoder_2_out3);

  // Notes on the sheet:
  //   contents of rom_1 (hex, n*v repeats v):
  //   5 8c10 0 8308 10 8c10 1 8308 2 fc10 10 f090 2 e308 1 fc98 c e306 0 ea87 c ea87
  //   c
  //   a
  //   x
  //   i
endmodule
