// Logisim project elements.circ as structural Verilog: 7 circuits, main circuit NAND
module NAND (
  input  a,
  input  b,
  output out
);

  nand nand_1 (out, a, b);
endmodule

module NOT (
  input  in,
  output out
);

  nand nand_1 (out, in, in);
endmodule

module AND (
  input  a,
  input  b,
  output out
);

  wire nand_1_out;

  nand nand_1 (nand_1_out, a, b);
  nand nand_2 (out, nand_1_out, nand_1_out);
endmodule

module OR (
  input  a,
  input  b,
  output out
);

  wire nand_1_out, nand_2_out;

  nand nand_1 (nand_1_out, a, a);
  nand nand_2 (nand_2_out, b, b);
  nand nand_3 (out, nand_1_out, nand_2_out);
endmodule

module XOR (
  input  a,
  input  b,
  output out
);

  wire nand_1_out, nand_2_out, nand_3_out, nand_4_out, nand_5_out;

  nand nand_1 (nand_1_out, a, b);
  nand nand_2 (nand_2_out, a, a);
  nand nand_3 (nand_3_out, b, b);
  nand nand_4 (nand_4_out, nand_2_out, nand_3_out);
  nand nand_5 (nand_5_out, nand_1_out, nand_4_out);
  nand nand_6 (out, nand_5_out, nand_5_out);

  // Notes on the sheet:
  //   NAND
  //   OR
  //   AND
endmodule

module MUX (
  input  a,
  input  sel,
  input  b,
  output out
);

  wire nand_1_out, nand_2_out, nand_3_out, nand_4_out, nand_5_out, nand_6_out, nand_7_out;

  nand nand_1 (nand_1_out, sel, sel);
  nand nand_2 (nand_2_out, a, nand_1_out);
  nand nand_3 (nand_3_out, sel, b);
  nand nand_4 (nand_4_out, nand_2_out, nand_2_out);
  nand nand_5 (nand_5_out, nand_3_out, nand_3_out);
  nand nand_6 (nand_6_out, nand_4_out, nand_4_out);
  nand nand_7 (nand_7_out, nand_5_out, nand_5_out);
  nand nand_8 (out, nand_6_out, nand_7_out);

  // Notes on the sheet:
  //   NOT
  //   AND
  //   AND
  //   OR
endmodule

module DMUX (
  input  sel,
  input  in,
  output a,
  output b
);

  wire nand_1_out, nand_2_out, nand_3_out;

  nand nand_1 (nand_1_out, sel, sel);
  nand nand_2 (nand_2_out, nand_1_out, in);
  nand nand_3 (nand_3_out, sel, in);
  nand nand_4 (a, nand_2_out, nand_2_out);
  nand nand_5 (b, nand_3_out, nand_3_out);

  // Notes on the sheet:
  //   NOT
  //   AND
  //   AND
endmodule
